// Logisim project t2.circ as structural Verilog: 2 circuits, main circuit main
module main (
  input  data_bit,
  input  [31:0] G,
  input  clk
);

  wire [31:0] bit_push_1_value_out, register_1_q;

  Register #(.width(32)) register_1 (.D(bit_push_1_value_out), .en(1'b1), .clk(clk), .Q(register_1_q));  // open: clr
  // XOR_Gate xor_1 has open pins: in0=G, in1=register_1_q, out=open
  Multiplexer #(.width(32), .enable("false")) multiplexer_1 ();  // open: in0, in1, out, sel
  bit_push bit_push_1 (.\bit (data_bit), .value_out(bit_push_1_value_out));  // open: value
endmodule

module bit_push (
  input  \bit ,
  input  [31:0] value,
  output [31:0] value_out
);


  assign value_out = {value[30:0], \bit };
endmodule
